// Logisim project BRUNOMACEDO_CPU_RISC.circ as structural Verilog: 16 circuits, main circuit Add_4
module Main (
);

  wire clock_1_out, not_1_out, not_2_out, Ovflw_q, Reset_out, ula_1_overflow, ula_1_zero,
       unidade_de_controle_1_clk_ac, unidade_de_controle_1_clk_pc, unidade_de_controle_1_clk_ram,
       unidade_de_controle_1_clk_rl, \unidade_de_controle_1_direção , unidade_de_controle_1_e,
       unidade_de_controle_1_load, unidade_de_controle_1_r_w, unidade_de_controle_1_rst_pc, Zero_q;
  wire [2:0] \unidade_de_controle_1_operação ;
  wire [3:0] multiplexador_2x1_1_s, PC_q, ram_1_data, registrador_ac_1_q, ula_1_out_6,
       \unidade_de_controle_1_b_endereços , unidade_de_controle_1_dados, unidade_de_controle_1_operando;
  wire [7:0] \registror_de_instruções_1_q , rom_1_data;

  not not_1 (not_1_out, unidade_de_controle_1_load);
  Counter #(.width(4), .max('hf)) PC (
    .load(unidade_de_controle_1_load), .D(unidade_de_controle_1_dados), .count(not_1_out), .Q(PC_q),
    .clk(unidade_de_controle_1_clk_pc), .clr(unidade_de_controle_1_rst_pc));  // open: carry
  unidade_de_controle unidade_de_controle_1 (
    .\B_Endereços (\unidade_de_controle_1_b_endereços ), .Operando(unidade_de_controle_1_operando),
    .\Direção (\unidade_de_controle_1_direção ), .E(unidade_de_controle_1_e),
    .\Operação (\unidade_de_controle_1_operação ), .\Instrução (\registror_de_instruções_1_q ),
    .Clock(clock_1_out), .Reset(Reset_out), .Rst_PC(unidade_de_controle_1_rst_pc),
    .clk_Rl(unidade_de_controle_1_clk_rl), .clk_PC(unidade_de_controle_1_clk_pc),
    .clk_AC(unidade_de_controle_1_clk_ac), .clk_RAM(unidade_de_controle_1_clk_ram),
    .Dados(unidade_de_controle_1_dados), .Overflow(Ovflw_q), .Zero(Zero_q),
    .Load(unidade_de_controle_1_load), .R_W(unidade_de_controle_1_r_w));
  Clock clock_1 (.out(clock_1_out));
  Button Reset (.out(Reset_out));
  // Probe on rom_1_data
  ROM #(.addrWidth(4)) rom_1 (.addr(PC_q), .data(rom_1_data));  // open: sel
  \Registror_de_instruções  \registror_de_instruções_1  (
    .in_2(rom_1_data), .Clock(unidade_de_controle_1_clk_rl), .Q(\registror_de_instruções_1_q ));
  // Probe on registrador_ac_1_q
  Multiplexador_2x1 multiplexador_2x1_1 (
    .E(unidade_de_controle_1_operando), .controle(unidade_de_controle_1_e), .D(ram_1_data),
    .S(multiplexador_2x1_1_s));
  ULA ula_1 (
    .D(\unidade_de_controle_1_direção ), .A(registrador_ac_1_q), .B(multiplexador_2x1_1_s),
    .Controle(\unidade_de_controle_1_operação ), .overflow(ula_1_overflow), .out_6(ula_1_out_6),
    .Zero(ula_1_zero));
  Registrador_AC registrador_ac_1 (.D(ula_1_out_6), .Clock(unidade_de_controle_1_clk_ac), .Q(registrador_ac_1_q));
  RAM #(.addrWidth(4), .dataWidth(4)) ram_1 (
    .addr(\unidade_de_controle_1_b_endereços ), .data(ram_1_data), .clk(unidade_de_controle_1_clk_ram),
    .ld(unidade_de_controle_1_r_w));  // open: sel, clr
  not not_2 (not_2_out, unidade_de_controle_1_r_w);
  // Probe on multiplexador_2x1_1_s
  Buffer buffer_1 (.in_2(not_2_out), .B(registrador_ac_1_q), .S(ram_1_data));
  D_Flip_Flop Ovflw (
    .clk(unidade_de_controle_1_clk_ac), .D(ula_1_overflow), .Q(Ovflw_q));  // open: Qn, preset, en, reset
  D_Flip_Flop Zero (.clk(unidade_de_controle_1_clk_ac), .D(ula_1_zero), .Q(Zero_q));  // open: Qn, preset, en, reset
  // Probe on registrador_ac_1_q

  // Notes on the sheet:
  //   contents of rom_1 (hex, n*v repeats v):
  //   0 f0 1 f1 10 31 d0 f2 11 f0 12 f1 e4
  //   3
  //   4
  //   5
  //   7
  //   8
  //   C
  //   F
  //   0
  //   000
  //   0
  //   MOV
  //   1
  //   1
  //   000
  //   MOV
  //   0
  //   ADD
  //   2
  //   001
  //   1
  //   001
  //   ADD
  //   0
  //   010
  //   SUB
  //   010
  //   1
  //   SUB
  //   0
  //   011
  //   6
  //   OR
  //   1
  //   OR
  //   011
  //   0
  //   100
  //   NOT
  //   100
  //   NOT
  //   1
  //   9
  //   101
  //   0
  //   A
  //   SHF
  //   1
  //   101
  //   B
  //   SHF
  //   0
  //   110
  //   JPZ
  //   JPO
  //   1
  //   110
  //   D
  //   0
  //   111
  //   GO
  //   E
  //   STR
  //   1
  //   111
  //   Instruction Set
  //   AC <= X
  //   AC <= M(X)
  //   AC <= AC+X
  //   AC <= AC+M(X)
  //   AC <= AC-X
  //   AC <= AC-M(X)
  //   AC <= AC OR X
  //   AC <= AC OR M(X)
  //   AC <= NOT X
  //   AC <= NOT M( X)
  //   AC <= AC << Q
  //   AC <= AC >> Q
  //   PC <= X SE FLAG Z
  //   PC <= X SE FLAG O
  //   PC <= X
  //   M(X) <= AC 
endmodule

module Add_4 (
  input  [3:0] B,
  input  [3:0] A,
  input  Vem_1,
  output Vai_1,
  output [3:0] S
);

  wire add_1_2_vai_1, add_1_3_vai_1, add_1_4_vai_1;

  Add_1 add_1_1 (.s(S[3]), .vai_1(Vai_1), .A(A[3]), .B(B[3]), .Vem_1(add_1_2_vai_1));
  Add_1 add_1_2 (.s(S[2]), .vai_1(add_1_2_vai_1), .A(A[2]), .B(B[2]), .Vem_1(add_1_3_vai_1));
  Add_1 add_1_3 (.s(S[1]), .vai_1(add_1_3_vai_1), .A(A[1]), .B(B[1]), .Vem_1(add_1_4_vai_1));
  Add_1 add_1_4 (.s(S[0]), .vai_1(add_1_4_vai_1), .A(A[0]), .B(B[0]), .Vem_1(Vem_1));
endmodule

module Add_1 (
  input  A,
  input  B,
  input  Vem_1,
  output s,
  output vai_1
);

  wire and_1_out, and_2_out, or_1_out, xor_1_out;

  xor xor_1 (xor_1_out, A, B);
  or or_1 (or_1_out, B, Vem_1);
  and and_1 (and_1_out, B, Vem_1);
  xor xor_2 (s, xor_1_out, Vem_1);
  and and_2 (and_2_out, or_1_out, A);
  or or_2 (vai_1, and_2_out, and_1_out);
endmodule

module Sub_1 (
  input  A,
  input  B,
  input  Vem_1,
  output s,
  output vai_1
);

  wire and_1_out, and_2_out, not_1_out, or_1_out, xor_1_out;

  not not_1 (not_1_out, A);
  xor xor_1 (xor_1_out, A, B);
  or or_1 (or_1_out, B, Vem_1);
  and and_1 (and_1_out, B, Vem_1);
  xor xor_2 (s, xor_1_out, Vem_1);
  and and_2 (and_2_out, or_1_out, not_1_out);
  or or_2 (vai_1, and_2_out, and_1_out);
endmodule

module Sub_4 (
  input  [3:0] B,
  input  [3:0] A,
  input  Vem_1,
  output Vai_1,
  output [3:0] S
);

  wire sub_1_2_vai_1, sub_1_3_vai_1, sub_1_4_vai_1;

  Sub_1 sub_1_1 (.A(A[3]), .B(B[3]), .Vem_1(sub_1_2_vai_1), .s(S[3]), .vai_1(Vai_1));
  Sub_1 sub_1_2 (.A(A[2]), .B(B[2]), .Vem_1(sub_1_3_vai_1), .s(S[2]), .vai_1(sub_1_2_vai_1));
  Sub_1 sub_1_3 (.A(A[1]), .B(B[1]), .Vem_1(sub_1_4_vai_1), .s(S[1]), .vai_1(sub_1_3_vai_1));
  Sub_1 sub_1_4 (.A(A[0]), .B(B[0]), .Vem_1(Vem_1), .s(S[0]), .vai_1(sub_1_4_vai_1));
endmodule

module Buffer (
  input  [3:0] B,
  input  in_2,
  output [3:0] S
);

  assign S[3] = in_2 ? B[3] : 1'bz;  // Controlled_Buffer controlled_buffer_1
  assign S[2] = in_2 ? B[2] : 1'bz;  // Controlled_Buffer controlled_buffer_2
  assign S[0] = in_2 ? B[0] : 1'bz;  // Controlled_Buffer controlled_buffer_3
  assign S[1] = in_2 ? B[1] : 1'bz;  // Controlled_Buffer controlled_buffer_4
endmodule

module Buffer_invertido (
  input  [3:0] B,
  input  in_2,
  output [3:0] S
);

  assign S[3] = in_2 ? ~B[3] : 1'bz;  // Controlled_Inverter controlled_inverter_1
  assign S[1] = in_2 ? ~B[1] : 1'bz;  // Controlled_Inverter controlled_inverter_2
  assign S[2] = in_2 ? ~B[2] : 1'bz;  // Controlled_Inverter controlled_inverter_3
  assign S[0] = in_2 ? ~B[0] : 1'bz;  // Controlled_Inverter controlled_inverter_4
endmodule

// Dec
module Decoder (
  input  [2:0] in_1,
  output S0,
  output S1,
  output S2,
  output S3,
  output S4,
  output S5,
  output S6,
  output S7
);

  wire not_1_out, not_2_out, not_3_out, not_4_out, not_5_out, not_6_out, not_7_out, not_8_out, not_9_out,
       not_10_out, not_11_out, not_12_out;

  not not_1 (not_1_out, in_1[2]);
  not not_2 (not_2_out, in_1[1]);
  not not_3 (not_3_out, in_1[0]);
  not not_4 (not_4_out, in_1[2]);
  not not_5 (not_5_out, in_1[1]);
  not not_6 (not_6_out, in_1[2]);
  not not_7 (not_7_out, in_1[0]);
  not not_8 (not_8_out, in_1[2]);
  not not_9 (not_9_out, in_1[1]);
  not not_10 (not_10_out, in_1[0]);
  not not_11 (not_11_out, in_1[1]);
  not not_12 (not_12_out, in_1[0]);
  and and_1 (S0, not_1_out, not_2_out, not_3_out);
  and and_2 (S1, not_4_out, not_5_out, in_1[0]);
  and and_3 (S2, not_6_out, in_1[1], not_7_out);
  and and_4 (S3, not_8_out, in_1[1], in_1[0]);
  and and_5 (S4, in_1[2], not_9_out, not_10_out);
  and and_6 (S5, in_1[2], not_11_out, in_1[0]);
  and and_7 (S6, in_1[2], in_1[1], not_12_out);
  and and_8 (S7, in_1[2], in_1[1], in_1[0]);
endmodule

module Rot_L (
  input  [3:0] ABCD,
  input  [1:0] XY,
  output [3:0] abcd_2
);

  wire and_1_out, and_2_out, and_3_out, and_4_out, and_5_out, and_6_out, and_7_out, and_8_out, and_9_out;

  and and_1 (and_1_out, ~XY[1], ~XY[0], ABCD[3]);  // AND_Gate
  and and_2 (and_2_out, ~XY[1], XY[0], ABCD[2]);  // AND_Gate
  and and_3 (and_3_out, XY[1], ~XY[0], ABCD[1]);  // AND_Gate
  and and_4 (and_4_out, XY[1], XY[0], ABCD[0]);
  and and_5 (and_5_out, ~XY[1], ~XY[0], ABCD[2]);  // AND_Gate
  and and_6 (and_6_out, ~XY[1], XY[0], ABCD[1]);  // AND_Gate
  and and_7 (and_7_out, XY[1], ~XY[0], ABCD[0]);  // AND_Gate
  and and_8 (and_8_out, ~XY[1], ~XY[0], ABCD[1]);  // AND_Gate
  and and_9 (and_9_out, ~XY[1], XY[0], ABCD[0]);  // AND_Gate
  and and_10 (abcd_2[0], ~XY[1], ~XY[0], ABCD[0]);  // AND_Gate
  or or_1 (abcd_2[3], and_1_out, and_2_out, and_3_out, and_4_out);
  or or_2 (abcd_2[2], and_5_out, and_6_out, and_7_out);
  or or_3 (abcd_2[1], and_8_out, and_9_out);
endmodule

module Rot_r (
  input  [3:0] ABCD,
  input  [1:0] XY,
  output [3:0] abcd_2
);

  wire and_1_out, and_2_out, and_3_out, and_4_out, and_5_out, and_6_out, and_7_out, and_8_out, and_9_out;

  and and_1 (and_1_out, ~XY[1], ~XY[0], ABCD[0]);  // AND_Gate
  and and_2 (and_2_out, ~XY[1], XY[0], ABCD[1]);  // AND_Gate
  and and_3 (and_3_out, XY[1], ~XY[0], ABCD[2]);  // AND_Gate
  and and_4 (and_4_out, XY[1], XY[0], ABCD[3]);
  and and_5 (and_5_out, ~XY[1], ~XY[0], ABCD[1]);  // AND_Gate
  and and_6 (and_6_out, ~XY[1], XY[0], ABCD[2]);  // AND_Gate
  and and_7 (and_7_out, XY[1], ~XY[0], ABCD[3]);  // AND_Gate
  and and_8 (and_8_out, ~XY[1], ~XY[0], ABCD[2]);  // AND_Gate
  and and_9 (and_9_out, ~XY[1], XY[0], ABCD[3]);  // AND_Gate
  and and_10 (abcd_2[3], ~XY[1], ~XY[0], ABCD[3]);  // AND_Gate
  or or_1 (abcd_2[0], and_1_out, and_2_out, and_3_out, and_4_out);
  or or_2 (abcd_2[1], and_5_out, and_6_out, and_7_out);
  or or_3 (abcd_2[2], and_8_out, and_9_out);
endmodule

module or_4_bits (
  input  [3:0] B,
  input  [3:0] A,
  output [3:0] S
);

  or or_1 (S[3], A[3], B[3]);
  or or_2 (S[1], A[1], B[1]);
  or or_3 (S[2], A[2], B[2]);
  or or_4 (S[0], A[0], B[0]);
endmodule

module ULA (
  input  D,
  input  [3:0] A,
  input  [3:0] B,
  input  [2:0] Controle,
  output overflow,
  output [3:0] out_6,
  output Zero
);

  wire add_4_1_vai_1, and_1_out, and_2_out, decoder_1_s0, decoder_1_s1, decoder_1_s2, decoder_1_s3,
       decoder_1_s4, decoder_1_s5, decoder_1_s6, decoder_1_s7, not_1_out, sub_4_1_vai_1;
  wire [3:0] add_4_1_s, buffer_5_s, or_4_bits_1_s, rot_l_1_abcd_2, rot_r_1_abcd_2, sub_4_1_s;

  or or_1 (overflow, and_1_out, and_2_out);
  and and_1 (and_1_out, add_4_1_vai_1, decoder_1_s1);
  and and_2 (and_2_out, sub_4_1_vai_1, decoder_1_s2);
  Decoder decoder_1 (
    .in_1(Controle), .S0(decoder_1_s0), .S1(decoder_1_s1), .S2(decoder_1_s2), .S3(decoder_1_s3),
    .S4(decoder_1_s4), .S5(decoder_1_s5), .S6(decoder_1_s6), .S7(decoder_1_s7));
  nor nor_1 (Zero, decoder_1_s7, decoder_1_s6, out_6[0], out_6[1], out_6[2], out_6[3]);
  Buffer buffer_1 (.in_2(decoder_1_s0), .B(B), .S(out_6));
  Add_4 add_4_1 (.A(B), .Vai_1(add_4_1_vai_1), .B(A), .Vem_1(1'b0), .S(add_4_1_s));
  Buffer buffer_2 (.in_2(decoder_1_s1), .B(add_4_1_s), .S(out_6));
  Sub_4 sub_4_1 (.A(A), .B(B), .Vem_1(1'b0), .Vai_1(sub_4_1_vai_1), .S(sub_4_1_s));
  Buffer buffer_3 (.in_2(decoder_1_s2), .B(sub_4_1_s), .S(out_6));
  or_4_bits or_4_bits_1 (.B(B), .S(or_4_bits_1_s), .A(A));
  Buffer buffer_4 (.in_2(decoder_1_s3), .B(or_4_bits_1_s), .S(out_6));
  Buffer_invertido buffer_invertido_1 (.B(B), .in_2(decoder_1_s4), .S(out_6));
  not not_1 (not_1_out, D);
  Rot_r rot_r_1 (.abcd_2(rot_r_1_abcd_2), .ABCD(A), .XY(B[1:0]));
  Rot_L rot_l_1 (.abcd_2(rot_l_1_abcd_2), .ABCD(A), .XY(B[1:0]));
  Buffer buffer_5 (.in_2(D), .B(rot_r_1_abcd_2), .S(buffer_5_s));
  Buffer buffer_6 (.in_2(not_1_out), .B(rot_l_1_abcd_2), .S(buffer_5_s));
  Buffer buffer_7 (.in_2(decoder_1_s5), .B(buffer_5_s), .S(out_6));
endmodule

module Registrador_AC (
  input  Clock,
  input  [3:0] D,
  output [3:0] Q
);

  D_Flip_Flop D3 (.clk(Clock), .D(D[3]), .Q(Q[3]));  // open: Qn, preset, en, reset
  D_Flip_Flop D2 (.clk(Clock), .D(D[2]), .Q(Q[2]));  // open: Qn, preset, en, reset
  D_Flip_Flop D1 (.clk(Clock), .D(D[1]), .Q(Q[1]));  // open: Qn, preset, en, reset
  D_Flip_Flop D0 (.clk(Clock), .D(D[0]), .Q(Q[0]));  // open: Qn, preset, en, reset
endmodule

module Multiplexador_2x1 (
  input  [3:0] E,
  input  [3:0] D,
  input  controle,
  output [3:0] S
);

  wire not_1_out;

  not not_1 (not_1_out, controle);
  Buffer buffer_1 (.in_2(not_1_out), .B(E), .S(S));
  Buffer buffer_2 (.in_2(controle), .B(D), .S(S));
endmodule

module \Registror_de_instruções  (
  input  Clock,
  input  [7:0] in_2,
  output [7:0] Q
);

  D_Flip_Flop D3 (.clk(Clock), .D(in_2[7]), .Q(Q[7]));  // open: Qn, preset, en, reset
  D_Flip_Flop D2 (.clk(Clock), .D(in_2[6]), .Q(Q[6]));  // open: Qn, preset, en, reset
  D_Flip_Flop D1 (.clk(Clock), .D(in_2[5]), .Q(Q[5]));  // open: Qn, preset, en, reset
  D_Flip_Flop D0 (.clk(Clock), .D(in_2[4]), .Q(Q[4]));  // open: Qn, preset, en, reset
  D_Flip_Flop D3_2 (.clk(Clock), .D(in_2[3]), .Q(Q[3]));  // open: Qn, preset, en, reset
  D_Flip_Flop D2_2 (.clk(Clock), .D(in_2[2]), .Q(Q[2]));  // open: Qn, preset, en, reset
  D_Flip_Flop D1_2 (.clk(Clock), .D(in_2[1]), .Q(Q[1]));  // open: Qn, preset, en, reset
  D_Flip_Flop D0_2 (.clk(Clock), .D(in_2[0]), .Q(Q[0]));  // open: Qn, preset, en, reset
endmodule

module unidade_de_controle (
  input  Clock,
  input  Reset,
  input  [7:0] \Instrução ,
  input  Zero,
  input  Overflow,
  output clk_Rl,
  output clk_AC,
  output clk_RAM,
  output [3:0] Dados,
  output clk_PC,
  output [3:0] \B_Endereços ,
  output Rst_PC,
  output [3:0] Operando,
  output \Direção ,
  output E,
  output [2:0] \Operação ,
  output R_W,
  output Load
);

  wire GoTo_out, JPO_out, JPZ_out, nand_1_out;
  wire [1:0] counter_1_q;

  nand Storage (R_W, \Instrução [7], \Instrução [6], \Instrução [5], \Instrução [4], clk_AC);
  Counter #(.width(2), .max('h3)) counter_1 (.Q(counter_1_q), .clk(Clock), .clr(Reset));  // open: load, D, count, carry
  and GoTo (GoTo_out, \Instrução [7], \Instrução [6], \Instrução [5], ~\Instrução [4], clk_PC);  // AND_Gate
  and and_1 (clk_Rl, ~counter_1_q[0], ~counter_1_q[1]);  // AND_Gate
  and JPO (JPO_out, \Instrução [7], \Instrução [6], ~\Instrução [5], \Instrução [4], clk_PC, Overflow);  // AND_Gate
  or or_1 (Load, GoTo_out, JPO_out, JPZ_out);
  and and_2 (clk_PC, counter_1_q[0], ~counter_1_q[1]);  // AND_Gate
  and JPZ (JPZ_out, \Instrução [7], \Instrução [6], ~\Instrução [5], ~\Instrução [4], clk_PC, Zero);  // AND_Gate
  and and_3 (clk_AC, ~counter_1_q[0], counter_1_q[1]);  // AND_Gate
  and and_4 (clk_RAM, counter_1_q[0], counter_1_q[1]);
  nand nand_1 (nand_1_out, \Instrução [7], ~\Instrução [6], \Instrução [5]);  // NAND_Gate
  and and_5 (E, \Instrução [4], nand_1_out);

  assign \B_Endereços  = \Instrução [3:0];
  assign Dados = \Instrução [3:0];
  assign \Direção  = \Instrução [4];
  assign Operando = \Instrução [3:0];
  assign \Operação  = \Instrução [7:5];
  assign Rst_PC = Reset;
endmodule
